// Logisim project CPU.circ as structural Verilog: 11 circuits, main circuit main
// 4
module main (
  input  [7:0] Testing_Data,
  input  OE_Testing_Data,
  input  OE,
  input  [3:0] OE_Testing_Data_2,
  input  [2:0] sel_Gattes,
  input  [1:0] sel_CBO,
  input  Enable_CBO,
  output [3:0] Count_Content,
  output [7:0] Instruction_Regsiter_Content,
  output [3:0] MAR_Content,
  output [7:0] MBR_Content,
  output [7:0] Regsiter_A_Content,
  output [7:0] Output_Register_Content,
  output [7:0] ALU_Result,
  output [2:0] Count_Content_2,
  output [7:0] C_B_O,
  output [7:0] Register_B_Content
);

  wire clock_1_out, cu_i_1_c0, cu_i_1_c1, cu_i_1_c2, cu_i_1_c3, cu_i_1_c4, cu_i_1_c5, cu_i_1_c6, cu_i_1_c7,
       cu_i_1_c8, cu_i_1_c9, cu_i_1_c10, cu_i_1_c11, cu_iitemp_1_c12, cu_iitemp_1_c13, cu_iitemp_1_c14,
       cu_iitemp_1_c15, cu_iitemp_1_c16, cu_iitemp_1_c17, undriven;
  wire [3:0] bitselector_2_out, controlled_buffer_1_out, MAR_dout;
  wire [7:0] alu_1_dout, bit_extender_1_out, bit_extender_2_out, Instruction_Register_dout;
  wire [31:0] Decimal_Decoder_2_dout, Decimal_Decoder_3_dout, Decimal_Decoder_4_dout, Decimal_Decoder_5_dout,
       Decimal_Decoder_dout;

  Clock clock_1 (.out(clock_1_out));
  Counter #(.width(4), .max('h4)) Program_Counter (
    .D(controlled_buffer_1_out), .count(cu_i_1_c1), .Q(Count_Content), .clk(clock_1_out));  // open: load, carry, clr
  Register Instruction_Register (
    .Clock(clock_1_out), .WE(cu_i_1_c7), .in_3(alu_1_dout), .OE(cu_i_1_c8), .Dout(Instruction_Register_dout),
    .Stored_Data(Instruction_Regsiter_Content));
  Decimal_Decoder Decimal_Decoder (.Din(Regsiter_A_Content), .Dout(Decimal_Decoder_dout));
  Register Register_A (
    .Clock(clock_1_out), .WE(cu_iitemp_1_c12), .in_3(alu_1_dout), .Stored_Data(Regsiter_A_Content));  // open: OE, Dout
  Register Register_B (
    .Clock(clock_1_out), .WE(cu_iitemp_1_c13), .in_3(alu_1_dout), .Stored_Data(Register_B_Content));  // open: OE, Dout
  Decimal_Decoder Decimal_Decoder_2 (.Din(Register_B_Content), .Dout(Decimal_Decoder_2_dout));
  assign controlled_buffer_1_out = cu_i_1_c0 ? Count_Content : 4'bz;  // Controlled_Buffer controlled_buffer_1
  assign bit_extender_1_out = {{4{1'b0}}, Count_Content};  // Bit_Extender bit_extender_1
  Decimal_Decoder Decimal_Decoder_3 (.Din(bit_extender_1_out), .Dout(Decimal_Decoder_3_dout));
  _7_Segment_Display u_7_segment_display_1 (
    .g(Decimal_Decoder_dout[11]), .f(Decimal_Decoder_dout[10]), .a(Decimal_Decoder_dout[9]),
    .b(Decimal_Decoder_dout[8]), .e(Decimal_Decoder_dout[27]), .d(Decimal_Decoder_dout[26]),
    .c(Decimal_Decoder_dout[25]), .dp(Decimal_Decoder_dout[24]));
  _7_Segment_Display u_7_segment_display_2 (
    .g(Decimal_Decoder_dout[15]), .f(Decimal_Decoder_dout[14]), .a(Decimal_Decoder_dout[13]),
    .b(Decimal_Decoder_dout[12]), .e(Decimal_Decoder_dout[31]), .d(Decimal_Decoder_dout[30]),
    .c(Decimal_Decoder_dout[29]), .dp(Decimal_Decoder_dout[28]));
  ALU alu_1 (
    .Sel_CBO(sel_CBO), .OE(cu_i_1_c11), .Sel_G(sel_Gattes), .REG_B(Register_B_Content),
    .REG_A(Regsiter_A_Content), .Enable(undriven), .Carry(C_B_O), .Dout(alu_1_dout), .Result(ALU_Result));
  _7_Segment_Display u_7_segment_display_3 (
    .g(Decimal_Decoder_2_dout[15]), .f(Decimal_Decoder_2_dout[14]), .a(Decimal_Decoder_2_dout[13]),
    .b(Decimal_Decoder_2_dout[12]), .e(Decimal_Decoder_2_dout[31]), .d(Decimal_Decoder_2_dout[30]),
    .c(Decimal_Decoder_2_dout[29]), .dp(Decimal_Decoder_2_dout[28]));
  _7_Segment_Display u_7_segment_display_4 (
    .g(Decimal_Decoder_2_dout[11]), .f(Decimal_Decoder_2_dout[10]), .a(Decimal_Decoder_2_dout[9]),
    .b(Decimal_Decoder_2_dout[8]), .e(Decimal_Decoder_2_dout[27]), .d(Decimal_Decoder_2_dout[26]),
    .c(Decimal_Decoder_2_dout[25]), .dp(Decimal_Decoder_2_dout[24]));
  _7_Segment_Display u_7_segment_display_5 (
    .g(Decimal_Decoder_3_dout[3]), .f(Decimal_Decoder_3_dout[2]), .a(Decimal_Decoder_3_dout[1]),
    .b(Decimal_Decoder_3_dout[0]), .e(Decimal_Decoder_3_dout[19]), .d(Decimal_Decoder_3_dout[18]),
    .c(Decimal_Decoder_3_dout[17]), .dp(Decimal_Decoder_3_dout[16]));
  _7_Segment_Display u_7_segment_display_6 (
    .g(Decimal_Decoder_dout[7]), .f(Decimal_Decoder_dout[6]), .a(Decimal_Decoder_dout[5]),
    .b(Decimal_Decoder_dout[4]), .e(Decimal_Decoder_dout[23]), .d(Decimal_Decoder_dout[22]),
    .c(Decimal_Decoder_dout[21]), .dp(Decimal_Decoder_dout[20]));
  _7_Segment_Display u_7_segment_display_7 (
    .g(Decimal_Decoder_dout[3]), .f(Decimal_Decoder_dout[2]), .a(Decimal_Decoder_dout[1]),
    .b(Decimal_Decoder_dout[0]), .e(Decimal_Decoder_dout[19]), .d(Decimal_Decoder_dout[18]),
    .c(Decimal_Decoder_dout[17]), .dp(Decimal_Decoder_dout[16]));
  _7_Segment_Display u_7_segment_display_8 (
    .g(Decimal_Decoder_2_dout[7]), .f(Decimal_Decoder_2_dout[6]), .a(Decimal_Decoder_2_dout[5]),
    .b(Decimal_Decoder_2_dout[4]), .e(Decimal_Decoder_2_dout[23]), .d(Decimal_Decoder_2_dout[22]),
    .c(Decimal_Decoder_2_dout[21]), .dp(Decimal_Decoder_2_dout[20]));
  _7_Segment_Display u_7_segment_display_9 (
    .g(Decimal_Decoder_2_dout[3]), .f(Decimal_Decoder_2_dout[2]), .a(Decimal_Decoder_2_dout[1]),
    .b(Decimal_Decoder_2_dout[0]), .e(Decimal_Decoder_2_dout[19]), .d(Decimal_Decoder_2_dout[18]),
    .c(Decimal_Decoder_2_dout[17]), .dp(Decimal_Decoder_2_dout[16]));
  BitSelector #(.group(4)) bitselector_1 (.in(Instruction_Register_dout), .out(controlled_buffer_1_out), .sel(1'b0));
  LED D2 (.in(alu_1_dout[5]));
  LED D0 (.in(alu_1_dout[7]));
  LED D1 (.in(alu_1_dout[6]));
  assign alu_1_dout = OE_Testing_Data ? Testing_Data : 8'bz;  // Controlled_Buffer controlled_buffer_2
  LED D5 (.in(alu_1_dout[2]));
  LED D4 (.in(alu_1_dout[3]));
  LED D3 (.in(alu_1_dout[4]));
  LED D6 (.in(alu_1_dout[1]));
  LED D7 (.in(alu_1_dout[0]));
  MAR MAR (
    .Clock(clock_1_out), .WE(cu_i_1_c9), .Din(controlled_buffer_1_out), .OE(cu_i_1_c10),
    .Reset(cu_iitemp_1_c17), .Dout(MAR_dout), .Stored_Data(MAR_Content));
  Register Output_Register (
    .Clock(clock_1_out), .WE(cu_iitemp_1_c15), .in_3(alu_1_dout), .OE(cu_iitemp_1_c14), .Dout(alu_1_dout),
    .Stored_Data(Output_Register_Content));
  assign alu_1_dout = cu_i_1_c5 ? MBR_Content : 8'bz;  // Controlled_Buffer controlled_buffer_3
  Decimal_Decoder Decimal_Decoder_4 (.Din(Output_Register_Content), .Dout(Decimal_Decoder_4_dout));
  assign MAR_dout = OE ? OE_Testing_Data_2 : 4'bz;  // Controlled_Buffer controlled_buffer_4
  Register MBR (
    .Clock(clock_1_out), .WE(cu_i_1_c4), .in_3(alu_1_dout), .OE(cu_i_1_c6), .Dout(alu_1_dout),
    .Stored_Data(MBR_Content));
  _7_Segment_Display u_7_segment_display_10 (
    .g(Decimal_Decoder_4_dout[15]), .f(Decimal_Decoder_4_dout[14]), .a(Decimal_Decoder_4_dout[13]),
    .b(Decimal_Decoder_4_dout[12]), .e(Decimal_Decoder_4_dout[31]), .d(Decimal_Decoder_4_dout[30]),
    .c(Decimal_Decoder_4_dout[29]), .dp(Decimal_Decoder_4_dout[28]));
  _7_Segment_Display u_7_segment_display_11 (
    .g(Decimal_Decoder_4_dout[7]), .f(Decimal_Decoder_4_dout[6]), .a(Decimal_Decoder_4_dout[5]),
    .b(Decimal_Decoder_4_dout[4]), .e(Decimal_Decoder_4_dout[23]), .d(Decimal_Decoder_4_dout[22]),
    .c(Decimal_Decoder_4_dout[21]), .dp(Decimal_Decoder_4_dout[20]));
  _7_Segment_Display u_7_segment_display_12 (
    .g(Decimal_Decoder_4_dout[11]), .f(Decimal_Decoder_4_dout[10]), .a(Decimal_Decoder_4_dout[9]),
    .b(Decimal_Decoder_4_dout[8]), .e(Decimal_Decoder_4_dout[27]), .d(Decimal_Decoder_4_dout[26]),
    .c(Decimal_Decoder_4_dout[25]), .dp(Decimal_Decoder_4_dout[24]));
  _7_Segment_Display u_7_segment_display_13 (
    .g(Decimal_Decoder_4_dout[3]), .f(Decimal_Decoder_4_dout[2]), .a(Decimal_Decoder_4_dout[1]),
    .b(Decimal_Decoder_4_dout[0]), .e(Decimal_Decoder_4_dout[19]), .d(Decimal_Decoder_4_dout[18]),
    .c(Decimal_Decoder_4_dout[17]), .dp(Decimal_Decoder_4_dout[16]));
  LED D1_2 (.in(alu_1_dout[6]));
  LED D0_2 (.in(alu_1_dout[7]));
  LED D2_2 (.in(alu_1_dout[5]));
  LED D3_2 (.in(alu_1_dout[4]));
  LED D5_2 (.in(alu_1_dout[2]));
  LED D4_2 (.in(alu_1_dout[3]));
  LED D6_2 (.in(alu_1_dout[1]));
  LED D7_2 (.in(alu_1_dout[0]));
  RAM #(.addrWidth(4), .bus("separate")) ram_1 (
    .addr(MAR_dout), .din(alu_1_dout), .data(alu_1_dout), .str(cu_i_1_c2), .clk(clock_1_out), .ld(cu_i_1_c3));  // open: sel, clr
  BitSelector #(.group(4)) bitselector_2 (.in(bit_extender_1_out), .out(bitselector_2_out), .sel(1'b0));
  Counter #(.width(3), .max('h5)) Step_Counter (
    .Q(Count_Content_2), .clk(clock_1_out), .clr(cu_iitemp_1_c16));  // open: load, D, count, carry
  CU_I cu_i_1 (
    .OPC3(bitselector_2_out[3]), .OPC2(bitselector_2_out[2]), .OPC1(bitselector_2_out[1]),
    .OPC0(bitselector_2_out[0]), .SC2(Count_Content_2[2]), .SC1(Count_Content_2[1]),
    .SC0(Count_Content_2[0]), .C0(cu_i_1_c0), .C1(cu_i_1_c1), .C2(cu_i_1_c2), .C3(cu_i_1_c3), .C4(cu_i_1_c4),
    .C5(cu_i_1_c5), .C6(cu_i_1_c6), .C7(cu_i_1_c7), .C8(cu_i_1_c8), .C9(cu_i_1_c9), .C10(cu_i_1_c10),
    .C11(cu_i_1_c11));
  CU_IItemp cu_iitemp_1 (
    .OPC3(bitselector_2_out[3]), .OPC2(bitselector_2_out[2]), .OPC1(bitselector_2_out[1]),
    .OPC0(bitselector_2_out[0]), .SC2(Count_Content_2[2]), .SC1(Count_Content_2[1]),
    .SC0(Count_Content_2[0]), .C12(cu_iitemp_1_c12), .C13(cu_iitemp_1_c13), .C14(cu_iitemp_1_c14),
    .C15(cu_iitemp_1_c15), .C16(cu_iitemp_1_c16), .C17(cu_iitemp_1_c17));
  assign bit_extender_2_out = {{5{1'b0}}, Count_Content_2};  // Bit_Extender bit_extender_2
  Decimal_Decoder Decimal_Decoder_5 (.Din(bit_extender_2_out), .Dout(Decimal_Decoder_5_dout));
  _7_Segment_Display u_7_segment_display_14 (
    .g(Decimal_Decoder_5_dout[3]), .f(Decimal_Decoder_5_dout[2]), .a(Decimal_Decoder_5_dout[1]),
    .b(Decimal_Decoder_5_dout[0]), .e(Decimal_Decoder_5_dout[19]), .d(Decimal_Decoder_5_dout[18]),
    .c(Decimal_Decoder_5_dout[17]), .dp(Decimal_Decoder_5_dout[16]));

  // Notes on the sheet:
  //   Internal Address Bus (4 Bits)
  //   Internal Data Bus
  //   External Address Bus
  //   External Data Bus
  //   Reset Counter
endmodule

module Memory_Cell (
  input  Clock,
  input  WE,
  input  Din,
  input  OE,
  input  Reset,
  output Dout,
  output Stored_Data
);

  wire and_1_out, and_2_out, not_1_out, or_1_out;

  not not_1 (not_1_out, WE);
  and and_1 (and_1_out, Stored_Data, not_1_out);
  and and_2 (and_2_out, WE, Din);
  or or_1 (or_1_out, and_1_out, and_2_out);
  D_Flip_Flop d_ff_1 (.clk(Clock), .D(or_1_out), .Q(Stored_Data), .reset(Reset));  // open: Qn, preset, en
  assign Dout = OE ? Stored_Data : 1'bz;  // Controlled_Buffer controlled_buffer_1

  // Notes on the sheet:
  //   Memory Cell
endmodule

module Register (
  input  Clock,
  input  WE,
  input  [7:0] in_3,
  input  OE,
  output [7:0] Dout,
  output [7:0] Stored_Data
);

  Memory_Cell _0 (
    .WE(WE), .Din(in_3[0]), .OE(OE), .Clock(Clock), .Dout(Dout[0]), .Stored_Data(Stored_Data[0]));  // open: Reset
  Memory_Cell _1 (
    .WE(WE), .Din(in_3[1]), .OE(OE), .Clock(Clock), .Dout(Dout[1]), .Stored_Data(Stored_Data[1]));  // open: Reset
  Memory_Cell _2 (
    .WE(WE), .Din(in_3[2]), .OE(OE), .Clock(Clock), .Dout(Dout[2]), .Stored_Data(Stored_Data[2]));  // open: Reset
  Memory_Cell _3 (
    .WE(WE), .Din(in_3[3]), .OE(OE), .Clock(Clock), .Dout(Dout[3]), .Stored_Data(Stored_Data[3]));  // open: Reset
  Memory_Cell _4 (
    .WE(WE), .Din(in_3[4]), .OE(OE), .Clock(Clock), .Dout(Dout[4]), .Stored_Data(Stored_Data[4]));  // open: Reset
  Memory_Cell _5 (
    .WE(WE), .Din(in_3[5]), .OE(OE), .Clock(Clock), .Dout(Dout[5]), .Stored_Data(Stored_Data[5]));  // open: Reset
  Memory_Cell _6 (
    .WE(WE), .Din(in_3[6]), .OE(OE), .Clock(Clock), .Dout(Dout[6]), .Stored_Data(Stored_Data[6]));  // open: Reset
  Memory_Cell _7 (
    .WE(WE), .Din(in_3[7]), .OE(OE), .Clock(Clock), .Dout(Dout[7]), .Stored_Data(Stored_Data[7]));  // open: Reset

  // Notes on the sheet:
  //   8 - bit Register 
endmodule

module MAR (
  input  Clock,
  input  WE,
  input  [3:0] Din,
  input  OE,
  input  Reset,
  output [3:0] Dout,
  output [3:0] Stored_Data
);

  Memory_Cell _0 (
    .WE(Din[0]), .Din(WE), .OE(OE), .Reset(Reset), .Clock(Clock), .Dout(Dout[0]), .Stored_Data(Stored_Data[0]));
  Memory_Cell _1 (
    .WE(Din[1]), .Din(WE), .OE(OE), .Reset(Reset), .Clock(Clock), .Dout(Dout[1]), .Stored_Data(Stored_Data[1]));
  Memory_Cell _2 (
    .WE(Din[2]), .Din(WE), .OE(OE), .Reset(Reset), .Clock(Clock), .Dout(Dout[2]), .Stored_Data(Stored_Data[2]));
  Memory_Cell _3 (
    .WE(Din[3]), .Din(WE), .OE(OE), .Reset(Reset), .Clock(Clock), .Dout(Dout[3]), .Stored_Data(Stored_Data[3]));
endmodule

module ALU (
  input  [7:0] REG_B,
  input  [7:0] REG_A,
  input  [1:0] Sel_CBO,
  input  Enable,
  input  OE,
  input  [2:0] Sel_G,
  output [7:0] Carry,
  output [7:0] Dout,
  output [7:0] Result
);

  wire [7:0] divider_1_out, divider_1_rem, multiplier_1_cout, multiplier_1_out, n8_bit_adder_1_cout,
       n8_bit_adder_1_sum, n8_bit_sub_1_borrow, n8_bit_sub_1_out_3, nand_1_out, nor_1_out, xnor_1_out,
       xor_1_out;

  _8_Bit_Adder u_8_bit_adder_1 (
    .A(REG_A), .B(REG_B), .Cin(1'b0), .Sum(n8_bit_adder_1_sum), .Cout(n8_bit_adder_1_cout[0]));
  _8_Bit_Sub u_8_bit_sub_1 (.A(REG_A), .B(REG_B), .out_3(n8_bit_sub_1_out_3), .Borrow(n8_bit_sub_1_borrow[0]));
  Multiplier multiplier_1 (.a(REG_A), .b(REG_B), .out(multiplier_1_out), .cout(multiplier_1_cout));  // open: cin
  Divider divider_1 (.a(REG_A), .b(REG_B), .out(divider_1_out), .rem(divider_1_rem));  // open: upper
  assign nand_1_out = ~(REG_A & REG_B);  // NAND_Gate nand_1, 8 bits wide
  assign nor_1_out = ~(REG_A | REG_B);  // NOR_Gate nor_1, 8 bits wide
  assign xor_1_out = REG_A ^ REG_B;  // XOR_Gate xor_1, 8 bits wide
  assign xnor_1_out = ~(REG_A ^ REG_B);  // XNOR_Gate xnor_1, 8 bits wide
  Multiplexer #(.select(3), .width(8)) multiplexer_1 (
    .in0(n8_bit_adder_1_sum), .in1(n8_bit_sub_1_out_3), .in2(multiplier_1_out), .in3(divider_1_out),
    .in4(nand_1_out), .in5(nor_1_out), .in6(xor_1_out), .in7(xnor_1_out), .out(Result), .sel(Sel_G));  // open: en
  assign Dout = OE ? Result : 8'bz;  // Controlled_Buffer controlled_buffer_1
  Multiplexer #(.select(2), .width(8)) multiplexer_2 (
    .in0(n8_bit_adder_1_cout), .in1(n8_bit_sub_1_borrow), .in2(multiplier_1_cout), .in3(divider_1_rem),
    .out(Carry), .sel(Sel_CBO), .en(Enable));
endmodule

module Decimal_Decoder (
  input  [7:0] Din,
  output [31:0] Dout
);

  ROM #(.dataWidth(32)) rom_1 (
    .addr(Din),
    .data({Dout[31:28], Dout[15:12], Dout[27:24], Dout[11:8], Dout[23:20], Dout[7:4], Dout[19:16], Dout[3:0]}));  // open: sel

  // Notes on the sheet:
  //   contents of rom_1 (hex, n*v repeats v):
  //   e7 21 cb 6b 2d 6e ee 23 ef 2f 21e7 2121 21cb 216b 212d 216e 21ee 2123 21ef 212f cbe7 cb21 cbcb cb6b
  //   cb2d cb6e cbee cb23 cbef cb2f 6be7 6b21 6bcb 6b6b 6b2d 6b6e 6bee 6b23 6bef 6b2f 2de7 2d21 2dcb 2d6b
  //   2d2d 2d6e 2dee 2d23 2def 2d2f 6ee7 6e21 6ecb 6e6b 6e2d 6e6e 6eee 6e23 6eef 6e2f eee7 ee21 eecb ee6b
  //   ee2d ee6e eeee ee23 eeef ee2f 23e7 2321 23cb 236b 232d 236e 23ee 2323 23ef 232f efe7 ef21 efcb ef6b
  //   ef2d ef6e efee ef23 efef ef2f 2fe7 2f21 2fcb 2f6b 2f2d 2f6e 2fee 2f23 2fef 2f2f 21e7e7 21e721 21e7cb
  //   21e76b 21e72d 21e76e 21e7ee 21e723 21e7ef 21e72f 2121e7 212121 2121cb 21216b 21212d 21216e 2121ee
  //   212123 2121ef 21212f 21cbe7 21cb21 21cbcb 21cb6b 21cb2d 21cb6e 21cbee 21cb23 21cbef 21cb2f 216be7
  //   216b21 216bcb 216b6b 216b2d 216b6e 216bee 216b23 216bef 216b2f 212de7 212d21 212dcb 212d6b 212d2d
  //   212d6e 212dee 212d23 212def 212d2f 216ee7 216e21 216ecb 216e6b 216e2d 216e6e 216eee 216e23 216eef
  //   216e2f 21eee7 21ee21 21eecb 21ee6b 21ee2d 21ee6e 21eeee 21ee23 21eeef 21ee2f 2123e7 212321 2123cb
  //   21236b 21232d 21236e 2123ee 212323 2123ef 21232f 21efe7 21ef21 21efcb 21ef6b 21ef2d 21ef6e 21efee
  //   21ef23 21efef 21ef2f 212fe7 212f21 212fcb 212f6b 212f2d 212f6e 212fee 212f23 212fef 212f2f cbe7e7
  //   cbe721 cbe7cb cbe76b cbe72d cbe76e cbe7ee cbe723 cbe7ef cbe72f cb21e7 cb2121 cb21cb cb216b cb212d
  //   cb216e cb21ee cb2123 cb21ef cb212f cbcbe7 cbcb21 cbcbcb cbcb6b cbcb2d cbcb6e cbcbee cbcb23 cbcbef
  //   cbcb2f cb6be7 cb6b21 cb6bcb cb6b6b cb6b2d cb6b6e cb6bee cb6b23 cb6bef cb6b2f cb2de7 cb2d21 cb2dcb
  //   cb2d6b cb2d2d cb2d6e cb2dee cb2d23 cb2def cb2d2f cb6ee7 cb6e21 cb6ecb cb6e6b cb6e2d cb6e6e
endmodule

module CU_I (
  input  OPC3,
  input  OPC2,
  input  OPC1,
  input  OPC0,
  input  SC2,
  input  SC1,
  input  SC0,
  output C0,
  output C1,
  output C2,
  output C3,
  output C4,
  output C5,
  output C6,
  output C7,
  output C8,
  output C9,
  output C10,
  output C11
);

  wire and_2_out, and_3_out, and_4_out, and_5_out, and_6_out, and_7_out, and_8_out, and_9_out, and_10_out,
       and_11_out, and_12_out, and_13_out, and_14_out, and_15_out, and_16_out, and_17_out, and_18_out,
       and_19_out, and_20_out, and_21_out, and_22_out, and_23_out, and_24_out, and_25_out, and_26_out,
       and_27_out, and_29_out, and_30_out, and_31_out, and_32_out, and_33_out, and_34_out, and_35_out,
       and_36_out, and_37_out, and_38_out, and_39_out, and_40_out, and_41_out, and_42_out, and_43_out,
       and_44_out, and_45_out, not_1_out, not_2_out, not_3_out, not_4_out, not_5_out, not_6_out, not_7_out,
       not_8_out, not_9_out, not_10_out, not_11_out, not_12_out, not_13_out, not_14_out, not_15_out,
       not_16_out, not_17_out, not_18_out, not_19_out, not_20_out, not_21_out, not_22_out, not_23_out,
       not_24_out, not_25_out, not_26_out, not_27_out, not_28_out, not_29_out, not_30_out, not_31_out,
       not_32_out, not_33_out, not_34_out, not_35_out, not_36_out, not_37_out, not_38_out, not_39_out,
       not_40_out, not_41_out, not_42_out, not_43_out, not_44_out, not_45_out, not_46_out, not_47_out,
       not_48_out, not_49_out, not_50_out, not_51_out, not_52_out, not_53_out, not_54_out, not_55_out,
       not_56_out, not_57_out, not_58_out, not_59_out, not_60_out, not_61_out, not_62_out, not_63_out,
       not_64_out, not_65_out, not_66_out, not_67_out, not_68_out, not_69_out, not_70_out, not_71_out,
       not_72_out, not_73_out, not_74_out, not_75_out, not_76_out, not_77_out, not_78_out, not_79_out,
       not_80_out, not_81_out, not_82_out, not_83_out, not_84_out, not_85_out, not_86_out, not_87_out,
       not_88_out, not_89_out, not_90_out, not_91_out, not_92_out, not_93_out, not_94_out, not_95_out,
       not_96_out, not_97_out, not_98_out, not_99_out, not_100_out, not_101_out, not_102_out, not_103_out,
       not_104_out, not_105_out, not_106_out, not_107_out, not_108_out, not_109_out, not_110_out,
       not_111_out, not_112_out, not_113_out, not_114_out, not_115_out, not_116_out, not_117_out,
       not_118_out, not_119_out, not_120_out, not_121_out, not_122_out, not_123_out, not_124_out;

  not not_1 (not_1_out, SC2);
  not not_2 (not_2_out, SC1);
  not not_3 (not_3_out, SC0);
  not not_4 (not_4_out, OPC3);
  not not_5 (not_5_out, OPC1);
  not not_6 (not_6_out, OPC0);
  not not_7 (not_7_out, SC2);
  not not_8 (not_8_out, SC1);
  not not_9 (not_9_out, OPC3);
  not not_10 (not_10_out, OPC1);
  not not_11 (not_11_out, OPC0);
  not not_12 (not_12_out, SC1);
  not not_13 (not_13_out, SC0);
  not not_14 (not_14_out, SC1);
  not not_15 (not_15_out, SC0);
  not not_16 (not_16_out, SC1);
  not not_17 (not_17_out, SC0);
  not not_18 (not_18_out, OPC3);
  not not_19 (not_19_out, OPC2);
  not not_20 (not_20_out, OPC0);
  not not_21 (not_21_out, SC1);
  not not_22 (not_22_out, SC0);
  not not_23 (not_23_out, OPC1);
  not not_24 (not_24_out, SC1);
  not not_25 (not_25_out, SC0);
  not not_26 (not_26_out, OPC1);
  not not_27 (not_27_out, SC1);
  not not_28 (not_28_out, SC0);
  not not_29 (not_29_out, OPC3);
  not not_30 (not_30_out, OPC2);
  not not_31 (not_31_out, OPC0);
  not not_32 (not_32_out, SC1);
  not not_33 (not_33_out, SC0);
  not not_34 (not_34_out, OPC1);
  not not_35 (not_35_out, SC1);
  not not_36 (not_36_out, SC0);
  not not_37 (not_37_out, OPC3);
  not not_38 (not_38_out, OPC1);
  not not_39 (not_39_out, OPC0);
  not not_40 (not_40_out, SC2);
  not not_41 (not_41_out, SC1);
  not not_42 (not_42_out, OPC1);
  not not_43 (not_43_out, SC1);
  not not_44 (not_44_out, SC0);
  not not_45 (not_45_out, SC1);
  not not_46 (not_46_out, OPC1);
  not not_47 (not_47_out, OPC0);
  not not_48 (not_48_out, SC2);
  not not_49 (not_49_out, SC0);
  not not_50 (not_50_out, OPC3);
  not not_51 (not_51_out, OPC2);
  not not_52 (not_52_out, OPC0);
  not not_53 (not_53_out, SC1);
  not not_54 (not_54_out, OPC1);
  not not_55 (not_55_out, SC1);
  not not_56 (not_56_out, SC2);
  not not_57 (not_57_out, SC0);
  not not_58 (not_58_out, SC2);
  not not_59 (not_59_out, SC0);
  not not_60 (not_60_out, OPC3);
  not not_61 (not_61_out, OPC2);
  not not_62 (not_62_out, SC2);
  not not_63 (not_63_out, SC0);
  not not_64 (not_64_out, OPC3);
  not not_65 (not_65_out, OPC2);
  not not_66 (not_66_out, SC2);
  not not_67 (not_67_out, SC0);
  not not_68 (not_68_out, OPC3);
  not not_69 (not_69_out, OPC1);
  not not_70 (not_70_out, OPC0);
  not not_71 (not_71_out, SC1);
  not not_72 (not_72_out, SC0);
  not not_73 (not_73_out, SC1);
  not not_74 (not_74_out, SC0);
  not not_75 (not_75_out, SC1);
  not not_76 (not_76_out, SC0);
  not not_77 (not_77_out, SC2);
  not not_78 (not_78_out, SC0);
  not not_79 (not_79_out, OPC3);
  not not_80 (not_80_out, OPC2);
  not not_81 (not_81_out, OPC0);
  not not_82 (not_82_out, SC2);
  not not_83 (not_83_out, OPC1);
  not not_84 (not_84_out, SC2);
  not not_85 (not_85_out, SC2);
  not not_86 (not_86_out, SC2);
  not not_87 (not_87_out, OPC3);
  not not_88 (not_88_out, OPC2);
  not not_89 (not_89_out, OPC0);
  not not_90 (not_90_out, SC2);
  not not_91 (not_91_out, OPC1);
  not not_92 (not_92_out, SC2);
  not not_93 (not_93_out, SC2);
  not not_94 (not_94_out, SC2);
  not not_95 (not_95_out, OPC3);
  not not_96 (not_96_out, OPC2);
  not not_97 (not_97_out, OPC0);
  not not_98 (not_98_out, SC1);
  not not_99 (not_99_out, SC0);
  not not_100 (not_100_out, OPC1);
  not not_101 (not_101_out, SC1);
  not not_102 (not_102_out, SC0);
  not not_103 (not_103_out, SC1);
  not not_104 (not_104_out, SC0);
  not not_105 (not_105_out, SC1);
  not not_106 (not_106_out, SC0);
  not not_107 (not_107_out, OPC3);
  not not_108 (not_108_out, OPC2);
  not not_109 (not_109_out, SC2);
  not not_110 (not_110_out, OPC0);
  not not_111 (not_111_out, SC2);
  not not_112 (not_112_out, OPC0);
  not not_113 (not_113_out, SC2);
  and and_1 (C0, not_1_out, not_2_out, not_3_out);
  not not_114 (not_114_out, SC2);
  not not_115 (not_115_out, SC1);
  and and_2 (and_2_out, not_114_out, not_115_out, SC0);
  and and_3 (and_3_out, not_4_out, OPC2, not_5_out, not_6_out, not_7_out, not_8_out);
  and and_4 (and_4_out, not_9_out, OPC2, not_10_out, not_11_out, SC2, not_12_out, not_13_out);
  and and_5 (and_5_out, OPC2, OPC1, OPC0, SC2, not_14_out, not_15_out);
  and and_6 (and_6_out, OPC3, OPC1, OPC0, SC2, not_16_out, not_17_out);
  not not_116 (not_116_out, SC2);
  not not_117 (not_117_out, SC1);
  and and_7 (and_7_out, not_116_out, not_117_out, SC0);
  and and_8 (and_8_out, not_18_out, not_19_out, not_20_out, SC2, not_21_out, not_22_out);
  and and_9 (and_9_out, not_23_out, OPC0, SC2, not_24_out, not_25_out);
  and and_10 (and_10_out, OPC3, not_26_out, SC2, not_27_out, not_28_out);
  not not_118 (not_118_out, SC2);
  not not_119 (not_119_out, SC1);
  and and_11 (and_11_out, not_118_out, not_119_out, SC0);
  and and_12 (and_12_out, not_29_out, not_30_out, not_31_out, SC2, not_32_out, not_33_out);
  and and_13 (and_13_out, not_34_out, OPC0, SC2, not_35_out, not_36_out);
  and and_14 (and_14_out, not_37_out, OPC2, not_38_out, not_39_out, not_40_out, SC0);
  and and_15 (and_15_out, OPC2, OPC1, OPC0, not_41_out, SC0);
  and and_16 (and_16_out, OPC3, not_42_out, SC2, not_43_out, not_44_out);
  and and_17 (and_17_out, OPC3, OPC1, OPC0, not_45_out, SC0);
  and and_18 (and_18_out, not_46_out, not_47_out, not_48_out, SC1, not_49_out);
  and and_19 (and_19_out, not_50_out, not_51_out, not_52_out, SC2, not_53_out, SC0);
  and and_20 (and_20_out, not_54_out, SC2, not_55_out, SC0);
  and and_21 (and_21_out, OPC2, not_56_out, SC1, not_57_out);
  and and_22 (and_22_out, OPC3, not_58_out, SC1, not_59_out);
  and and_23 (and_23_out, not_60_out, not_61_out, OPC0, not_62_out, SC1, not_63_out);
  and and_24 (and_24_out, not_64_out, not_65_out, OPC1, not_66_out, SC1, not_67_out);
  and and_25 (and_25_out, not_68_out, OPC2, not_69_out, not_70_out, SC2, not_71_out, not_72_out);
  and and_26 (and_26_out, OPC2, OPC1, OPC0, SC2, not_73_out, not_74_out);
  and and_27 (and_27_out, OPC3, OPC1, OPC0, SC2, not_75_out, not_76_out);
  and and_28 (C7, not_77_out, SC1, not_78_out);
  and and_29 (and_29_out, not_79_out, not_80_out, not_81_out, not_82_out, SC1, SC0);
  and and_30 (and_30_out, not_83_out, not_84_out, SC1, SC0);
  and and_31 (and_31_out, OPC2, OPC0, not_85_out, SC1, SC0);
  and and_32 (and_32_out, OPC3, OPC0, not_86_out, SC1, SC0);
  not not_120 (not_120_out, SC2);
  and and_33 (and_33_out, not_120_out, not_121_out, not_122_out);
  not not_121 (not_121_out, SC1);
  not not_122 (not_122_out, SC0);
  and and_34 (and_34_out, not_87_out, not_88_out, not_89_out, not_90_out, SC1, SC0);
  and and_35 (and_35_out, not_91_out, not_92_out, SC1, SC0);
  and and_36 (and_36_out, OPC2, OPC0, not_93_out, SC1, SC0);
  and and_37 (and_37_out, OPC3, OPC0, not_94_out, SC1, SC0);
  not not_123 (not_123_out, SC2);
  not not_124 (not_124_out, SC1);
  and and_38 (and_38_out, not_123_out, not_124_out, SC0);
  and and_39 (and_39_out, not_95_out, not_96_out, not_97_out, SC2, not_98_out, not_99_out);
  and and_40 (and_40_out, not_100_out, SC2, not_101_out, not_102_out);
  and and_41 (and_41_out, OPC2, OPC0, SC2, not_103_out, not_104_out);
  and and_42 (and_42_out, OPC3, OPC0, SC2, not_105_out, not_106_out);
  and and_43 (and_43_out, not_107_out, not_108_out, OPC1, OPC0, not_109_out, SC1, SC0);
  and and_44 (and_44_out, OPC2, OPC1, not_110_out, not_111_out, SC1, SC0);
  and and_45 (and_45_out, OPC3, OPC1, not_112_out, not_113_out, SC1, SC0);
  or or_1 (C1, and_2_out, and_3_out);
  or or_2 (C2, and_4_out, and_5_out, and_6_out);
  or or_3 (C3, and_7_out, and_8_out, and_9_out, and_10_out);
  or or_4 (C5, and_18_out, and_19_out, and_20_out, and_21_out, and_22_out);
  or or_5 (C6, and_23_out, and_24_out, and_25_out, and_26_out, and_27_out);
  or or_6 (C8, and_29_out, and_30_out, and_31_out, and_32_out);
  or or_7 (C9, and_33_out, and_34_out, and_35_out, and_36_out, and_37_out);
  or or_8 (C10, and_38_out, and_39_out, and_40_out, and_41_out, and_42_out);
  or or_9 (C11, and_43_out, and_44_out, and_45_out);
  or or_10 (C4, and_11_out, and_12_out, and_13_out, and_14_out, and_15_out, and_16_out, and_17_out);
endmodule

module CU_IItemp (
  input  OPC3,
  input  OPC2,
  input  OPC1,
  input  OPC0,
  input  SC2,
  input  SC1,
  input  SC0,
  output C12,
  output C13,
  output C14,
  output C15,
  output C16,
  output C17
);

  wire and_1_out, and_2_out, and_3_out, and_4_out, and_5_out, and_6_out, and_7_out, and_8_out, and_9_out,
       and_10_out, and_11_out, and_12_out, and_13_out, and_14_out, and_15_out, and_16_out, and_17_out,
       and_18_out, not_1_out, not_2_out, not_3_out, not_4_out, not_5_out, not_6_out, not_7_out, not_8_out,
       not_9_out, not_10_out, not_11_out, not_12_out, not_13_out, not_14_out, not_15_out, not_16_out,
       not_17_out, not_18_out, not_19_out, not_20_out, not_21_out, not_22_out, not_23_out, not_24_out,
       not_25_out, not_26_out, not_27_out, not_28_out, not_29_out, not_30_out, not_31_out, not_32_out,
       not_33_out, not_34_out, not_35_out, not_36_out, not_37_out, not_38_out, not_39_out, not_40_out,
       not_41_out, not_42_out, not_43_out, not_44_out, not_45_out, not_46_out, not_47_out, not_48_out,
       not_49_out, not_50_out, not_51_out, not_52_out, not_53_out, not_54_out, not_55_out, not_56_out,
       not_57_out;

  not not_1 (not_1_out, OPC3);
  not not_2 (not_2_out, OPC2);
  not not_3 (not_3_out, OPC1);
  not not_4 (not_4_out, SC1);
  not not_5 (not_5_out, OPC1);
  not not_6 (not_6_out, OPC0);
  not not_7 (not_7_out, SC1);
  not not_8 (not_8_out, OPC3);
  not not_9 (not_9_out, OPC2);
  not not_10 (not_10_out, OPC0);
  not not_11 (not_11_out, SC1);
  not not_12 (not_12_out, OPC1);
  not not_13 (not_13_out, SC1);
  not not_14 (not_14_out, OPC1);
  not not_15 (not_15_out, SC1);
  not not_16 (not_16_out, OPC3);
  not not_17 (not_17_out, OPC1);
  not not_18 (not_18_out, OPC0);
  not not_19 (not_19_out, SC2);
  not not_20 (not_20_out, SC2);
  not not_21 (not_21_out, SC2);
  not not_22 (not_22_out, OPC2);
  not not_23 (not_23_out, OPC0);
  not not_24 (not_24_out, SC2);
  not not_25 (not_25_out, OPC3);
  not not_26 (not_26_out, OPC2);
  not not_27 (not_27_out, SC2);
  not not_28 (not_28_out, OPC0);
  not not_29 (not_29_out, SC2);
  not not_30 (not_30_out, OPC0);
  not not_31 (not_31_out, SC2);
  not not_32 (not_32_out, OPC3);
  not not_33 (not_33_out, OPC2);
  not not_34 (not_34_out, SC1);
  not not_35 (not_35_out, SC0);
  not not_36 (not_36_out, OPC3);
  not not_37 (not_37_out, OPC1);
  not not_38 (not_38_out, OPC0);
  not not_39 (not_39_out, SC1);
  not not_40 (not_40_out, OPC3);
  not not_41 (not_41_out, OPC2);
  not not_42 (not_42_out, OPC1);
  not not_43 (not_43_out, SC1);
  not not_44 (not_44_out, OPC3);
  not not_45 (not_45_out, OPC2);
  not not_46 (not_46_out, OPC0);
  not not_47 (not_47_out, SC1);
  not not_48 (not_48_out, OPC3);
  not not_49 (not_49_out, OPC2);
  not not_50 (not_50_out, SC2);
  not not_51 (not_51_out, SC0);
  not not_52 (not_52_out, OPC3);
  not not_53 (not_53_out, OPC1);
  not not_54 (not_54_out, OPC0);
  not not_55 (not_55_out, SC2);
  not not_56 (not_56_out, SC1);
  not not_57 (not_57_out, SC0);
  and and_1 (and_1_out, not_1_out, not_2_out, not_3_out, SC2, not_4_out, SC0);
  and and_2 (and_2_out, not_5_out, not_6_out, SC2, not_7_out, SC0);
  and and_3 (and_3_out, not_8_out, not_9_out, OPC1, not_10_out, SC2, not_11_out, SC0);
  and and_4 (and_4_out, OPC2, not_12_out, OPC0, SC2, not_13_out, SC0);
  and and_5 (and_5_out, OPC3, not_14_out, OPC0, SC2, not_15_out, SC0);
  and and_6 (and_6_out, not_16_out, OPC2, not_17_out, not_18_out, not_19_out, SC1, SC0);
  and and_7 (and_7_out, OPC2, OPC1, OPC0, not_20_out, SC1, SC0);
  and and_8 (and_8_out, OPC3, OPC1, OPC0, not_21_out, SC1, SC0);
  and and_9 (and_9_out, not_22_out, not_23_out, not_24_out, SC1, SC0);
  and and_10 (and_10_out, not_25_out, not_26_out, OPC1, not_27_out, SC1, SC0);
  and and_11 (and_11_out, OPC1, not_28_out, not_29_out, SC1, SC0);
  and and_12 (and_12_out, OPC3, not_30_out, not_31_out, SC1, SC0);
  and and_13 (and_13_out, not_32_out, not_33_out, OPC1, OPC0, SC2, not_34_out, not_35_out);
  and and_14 (and_14_out, not_36_out, OPC2, not_37_out, not_38_out, SC2, not_39_out, SC0);
  and and_15 (and_15_out, not_40_out, not_41_out, not_42_out, OPC0, SC2, not_43_out, SC0);
  and and_16 (and_16_out, not_44_out, not_45_out, OPC1, not_46_out, SC2, not_47_out, SC0);
  and and_17 (and_17_out, not_48_out, not_49_out, OPC1, OPC0, not_50_out, SC1, not_51_out);
  and and_18 (and_18_out, not_52_out, OPC2, not_53_out, not_54_out, not_55_out, not_56_out, not_57_out);
  or or_1 (C12, and_1_out, and_2_out);
  or or_2 (C13, and_3_out, and_4_out, and_5_out);
  or or_3 (C14, and_6_out, and_7_out, and_8_out);
  or or_4 (C15, and_9_out, and_10_out, and_11_out, and_12_out);
  or or_5 (C16, and_13_out, and_14_out);
  or or_6 (C17, and_15_out, and_16_out, and_17_out, and_18_out);
endmodule

module Adder (
  input  A,
  input  B,
  input  Cin,
  output Sum,
  output Cout
);

  wire and_1_out, and_2_out, xor_1_out;

  xor xor_1 (xor_1_out, A, B);
  and and_1 (and_1_out, A, B);
  xor xor_2 (Sum, xor_1_out, Cin);
  and and_2 (and_2_out, xor_1_out, Cin);
  or or_1 (Cout, and_2_out, and_1_out);
endmodule

module _8_Bit_Adder (
  input  [7:0] A,
  input  [7:0] B,
  input  Cin,
  output [7:0] Sum,
  output Cout
);

  wire adder_1_cout, adder_2_cout, adder_3_cout, adder_4_cout, adder_5_cout, adder_6_cout, adder_7_cout;

  Adder adder_1 (.A(A[0]), .B(B[0]), .Cin(Cin), .Sum(Sum[0]), .Cout(adder_1_cout));
  Adder adder_2 (.A(A[1]), .B(B[1]), .Cin(adder_1_cout), .Sum(Sum[1]), .Cout(adder_2_cout));
  Adder adder_3 (.A(A[2]), .B(B[2]), .Cin(adder_2_cout), .Sum(Sum[2]), .Cout(adder_3_cout));
  Adder adder_4 (.A(A[4]), .B(B[4]), .Cin(adder_5_cout), .Sum(Sum[4]), .Cout(adder_4_cout));
  Adder adder_5 (.A(A[3]), .B(B[3]), .Cin(adder_3_cout), .Sum(Sum[3]), .Cout(adder_5_cout));
  Adder adder_6 (.A(A[5]), .B(B[5]), .Cin(adder_4_cout), .Sum(Sum[5]), .Cout(adder_6_cout));
  Adder adder_7 (.A(A[6]), .B(B[6]), .Cin(adder_6_cout), .Sum(Sum[6]), .Cout(adder_7_cout));
  Adder adder_8 (.A(A[7]), .B(B[7]), .Cin(adder_7_cout), .Sum(Sum[7]), .Cout(Cout));
endmodule

module _8_Bit_Sub (
  input  [7:0] A,
  input  [7:0] B,
  output [7:0] out_3,
  output Borrow
);

  wire n8_bit_adder_1_cout;
  wire [7:0] not_1_out;

  assign not_1_out = ~B;  // NOT_Gate not_1, 8 bits wide
  _8_Bit_Adder u_8_bit_adder_1 (.A(A), .B(not_1_out), .Cin(1'b1), .Sum(out_3), .Cout(n8_bit_adder_1_cout));
  not not_2 (Borrow, n8_bit_adder_1_cout);
endmodule
